# Fritzing sketch LCD_shield_with_thermistor (saved by Fritzing 0.9.10b)
breadboards: 1

parts:
  U1 = Arduino Uno (Rev3)
  LCD1 = LCD screen
  R1 = Resistor [tolerance=±5% power=0.25 resistance=10k package=THT]
  R2 = Temperature Sensor (Thermistor) [thermistor_type=NTC package=THT]
  R3_Contrast_Adj = Trimmer Potentiometer [maximum_resistance=10kΩ knob_status=50% power=0.5W package=THT]
  Q1 = NPN-Transistor [part_number=9013 package="TO92 [THT]"]
  R4 = Resistor [tolerance=±5% power=0.25 resistance=4.7k package=THT]
  R5 = Resistor [tolerance=±5% power=0.25 resistance=10k package=THT]

nets:
  LCD Push buttons: U1.A0
  N1: U1.A1, R1.Pin_1, R2.pin_1
  N2: U1.D8, LCD1.RS
  N3: U1.D9_PWM, LCD1.E
  N4: U1.D10_PWM/SS, R4.Pin_1, R5.Pin_1
  N5: U1.GND, R2.pin_0
  N6: U1.D4, LCD1.DB4
  N7: U1.D5_PWM, LCD1.DB5
  N8: U1.D6_PWM, LCD1.DB6
  N9: U1.D7, LCD1.DB7
  5V: U1.5V, LCD1.VDD, LCD1.LED+, R1.Pin_0, R3_Contrast_Adj.leg1, R4.Pin_0
  GND: LCD1.VSS, LCD1.R/W, R3_Contrast_Adj.leg2, Q1.E
  N10: LCD1.V0, R3_Contrast_Adj.wiper
  N11: LCD1.LED-, Q1.C
  N12: Q1.B, R5.Pin_0
